# Fritzing sketch MosfetLED_circuit (saved by Fritzing 0.8.3b)
breadboards: 1

parts:
  R1 = Resistor [tolerance=±5% resistance=100 package=THT]
  Q2 = Basic FET N-Channel [package="TO220 [THT]"]
  R2 = Resistor [tolerance=±5% resistance=100 package=THT]
  Q3 = Basic FET N-Channel [package="TO220 [THT]"]
  R3 = Resistor [tolerance=±5% resistance=100 package=THT]
  Q1 = Basic FET N-Channel [package="TO220 [THT]"]
  RGB_LED_(common_anode) = RGB LED (com. anode, rbg) [package="5 mm [THT]"]

nets:
  GND: R1.Pin_0, Q2.source, R2.Pin_1, Q3.source, R3.Pin_0, Q1.source
  Pin 3: R1.Pin_1, Q1.gate
  Pin 4: Q2.gate, R3.Pin_1
  N1: Q2.drain, RGB_LED_(common_anode).red_cathode
  Pin 2: R2.Pin_0, Q3.gate
  N2: Q3.drain, RGB_LED_(common_anode).blue_cathode
  N3: Q1.drain, RGB_LED_(common_anode).green_cathode
  12V: RGB_LED_(common_anode).common_anode
