# Fritzing sketch full_circuit (saved by Fritzing 0.8.3b)
breadboards: 1

parts:
  Part1 = Arduino Mega 2560 (Rev3)
  Q1 = Basic FET N-Channel [package="TO220 [THT]"]
  R1 = Resistor [tolerance=±5% resistance=100 package=THT]
  Q2 = Basic FET N-Channel [package="TO220 [THT]"]
  R2 = Resistor [tolerance=±5% resistance=100 package=THT]
  Q3 = Basic FET N-Channel [package="TO220 [THT]"]
  R3 = Resistor [tolerance=±5% resistance=100 package=THT]
  SONAR1 = Maxbotix MaxSonar Ultrasonic Sensor (Hi-Res) [part_number="Maxbotix HRLV-EZ1"]
  IR1 = TSOP312.., 314.. [part_number="IR Receiver Diode - SEN-10266" package=THT]
  Part2 = Arduino Pro Mini v13

nets:
  N1: Part1.D19/RX1, Part2.D0/TX
  N2: Part1.D17_PWM/RX2, SONAR1.TX
  GND: Part1.GND, Q1.source, R1.Pin_0, Q2.source, R2.Pin_0, Q3.source, R3.Pin_0, SONAR1.GND, IR1.GND, Part2.GND
  N3: Part1.D2_PWM, Q3.gate, R3.Pin_1
  N4: Part1.D3_PWM, Q2.gate, R2.Pin_1
  N5: Part1.D4_PWM, Q1.gate, R1.Pin_1
  Red: Q1.drain
  Green: Q2.drain
  Blue: Q3.drain
  5V: SONAR1.+5V, IR1.Vs, Part2.VCC
  N6: IR1.Data, Part2.D2

notes:
  To RGB LED Strip
  +12V
  G
  R
  B

custom parts:
  Maxbotix MaxSonar Ultrasonic Sensor (Hi-Res): Maxbotix MaxSonar Hi-Resolution Ultrasonic Sensor HRLV-EZ0, HRLV-EZ1, HRLV-EZ2, HRLV-EZ3, HRLV-EZ4
